# Fritzing sketch board_env_variants (saved by Fritzing 1.0.6)

parts:
  U1 = ESP8266 NodeMCU LoLin module
  J1 = Piezo Speaker
  J2 = Piezo Speaker
  esp2 = ESP32 DevKitc V4
  Part9 = 4x Matrix LED 8x8 with MAX7219 [part_number=FC-16]
  Part10 = 4x Matrix LED 8x8 with MAX7219 [part_number=FC-16]
  WeMos_D1_Mini1 = WeMos D1 Mini
  J3 = Piezo Speaker
  Part11 = 4x Matrix LED 8x8 with MAX7219 [part_number=FC-16]
  Part12 = 4x Matrix LED 8x8 with MAX7219 [part_number=FC-16]
  Part13 = 4x Matrix LED 8x8 with MAX7219 [part_number=FC-16]
  J4 = Piezo Speaker
  WeMos_D1_Mini2 = WeMos D1 Mini
  U2 = ESP8266 NodeMCU LoLin module
  J5 = Piezo Speaker
  Part15 = 4x Matrix LED 8x8 with MAX7219 [part_number=FC-16]
  Part16 = 4x Matrix LED 8x8 with MAX7219 [part_number=FC-16]
  J6 = Piezo Speaker
  esp3 = ESP32 DevKitc V4
  Part18 = 4x Matrix LED 8x8 with MAX7219 [part_number=FC-16]
  Part19 = 4x Matrix LED 8x8 with MAX7219 [part_number=FC-16]

nets:
  N1: U1.D1, J1.pin2
  3V3: U1.3V3, Part9.VCC
  GND: U1.GND, J1.pin1, Part9.GND
  N2: U1.D5, Part9.CLK
  N3: U1.D7, Part9.DIN
  N4: U1.D8, Part9.CS
  N5: J2.pin1, esp2.GND#12
  N6: J2.pin2, esp2.IO4
  N7: esp2.IO5, Part10.CS
  N8: esp2.IO18, Part10.CLK
  N9: esp2.IO23, Part10.DIN
  3V3_2: esp2.3V3, Part10.VCC
  N10: esp2.GND#32, Part10.GND
  3V3_3: WeMos_D1_Mini1.3V3, Part11.VCC
  N11: WeMos_D1_Mini1.D1, J3.pin2
  N12: WeMos_D1_Mini1.D4, Part11.CS
  N13: WeMos_D1_Mini1.D5, Part11.CLK
  N14: WeMos_D1_Mini1.D7, Part11.DIN
  N15: WeMos_D1_Mini1.G, J3.pin1, Part11.GND
  N16: Part12.VCC#0, WeMos_D1_Mini2.3V3
  N17: Part12.GND#1, J4.pin1, WeMos_D1_Mini2.G
  N18: Part12.CS, WeMos_D1_Mini2.D4
  N19: Part12.CLK, WeMos_D1_Mini2.D5
  N20: Part12.DIN, WeMos_D1_Mini2.D7
  N21: Part12.VCC#5, Part13.VCC
  N22: Part12.GND#6, Part13.GND
  N23: Part12.CS(OUT), Part13.CS
  N24: Part12.CLK(OUT), Part13.CLK
  N25: Part12.DOUT, Part13.DIN
  N26: J4.pin2, WeMos_D1_Mini2.D1
  N27: U2.D1, J5.pin2
  N28: U2.3V3, Part15.VCC#0
  N29: U2.GND, J5.pin1, Part15.GND#1
  N30: U2.D5, Part15.CLK
  N31: U2.D7, Part15.DIN
  N32: U2.D8, Part15.CS
  N33: Part15.VCC#5, Part16.VCC
  N34: Part15.GND#6, Part16.GND
  N35: Part15.CS(OUT), Part16.CS
  N36: Part15.CLK(OUT), Part16.CLK
  N37: Part15.DOUT, Part16.DIN
  N38: J6.pin1, esp3.GND#12
  N39: J6.pin2, esp3.IO4
  N40: esp3.IO5, Part18.CS
  N41: esp3.IO18, Part18.CLK
  N42: esp3.IO23, Part18.DIN
  N43: esp3.3V3, Part18.VCC#0
  N44: esp3.GND#32, Part18.GND#1
  N45: Part18.VCC#5, Part19.VCC
  N46: Part18.GND#6, Part19.GND
  N47: Part18.CS(OUT), Part19.CS
  N48: Part18.CLK(OUT), Part19.CLK
  N49: Part18.DOUT, Part19.DIN

custom parts:
  ESP8266 NodeMCU LoLin module: ESP8266 based NodeMCU
  ESP32 DevKitc V4: ESP32-DevKitC board with ESP32-WROOM-32 module. ESP32-DevKitC V4 is a small-sized ESP32-based development board produced by Espressif. Most of the pins on the ESP module are broken out to the pin headers on the board. The pins D0, D1, D2, D3, CMD and CLK are used internally for communication between ESP32 and SPI flash memory. They are grouped on both sides near the USB connector. Avoid using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
  4x Matrix LED 8x8 with MAX7219: FC-16
